// Logisim project Z80.circ as structural Verilog
module ALU (
  input  [7:0] DataIN,
  input  [3:0] ALUCtl,
  input  CLK,
  input  RESET,
  output [7:0] DataOut
);

  wire not_1_out;
  wire [7:0] adder_1_out, adder_2_out, ALUBuffer_q, and_1_out, multiplexer_1_out, negator_1_out, not_2_out,
       or_1_out, xor_1_out;

  not not_1 (not_1_out, ALUCtl[3]);
  Register ALUBuffer (.D(DataIN), .en(not_1_out), .clk(CLK), .Q(ALUBuffer_q), .clr(RESET));
  Adder adder_1 (.a(8'h1), .b(DataIN), .out(adder_1_out));  // open: cin, cout
  Adder adder_2 (.a(ALUBuffer_q), .b(DataIN), .out(adder_2_out));  // open: cin, cout
  Negator negator_1 (.in(DataIN), .out(negator_1_out));
  assign and_1_out = ALUBuffer_q & DataIN;  // AND_Gate and_1, 8 bits wide
  assign or_1_out = ALUBuffer_q | DataIN;  // OR_Gate or_1, 8 bits wide
  assign xor_1_out = ALUBuffer_q ^ DataIN;  // XOR_Gate xor_1, 8 bits wide
  assign not_2_out = ~DataIN;  // NOT_Gate not_2, 8 bits wide
  Multiplexer #(.select(3), .width(8)) multiplexer_1 (
    .in0(adder_1_out), .in1(adder_2_out), .in2(negator_1_out), .in3(and_1_out), .in4(or_1_out),
    .in5(xor_1_out), .in6(not_2_out), .in7(8'h1), .out(multiplexer_1_out), .sel(ALUCtl[2:0]));
  ACC acc_1 (.Data(multiplexer_1_out), .Enable(ALUCtl[3]), .CLK(CLK), .RESET(RESET), .DataOut(DataOut));

  // Other names for the same wires on the sheet: ALUCtl_t[2:0] = ALUCtl[2:0]; ACCEna = ALUCtl[3]

  // Notes on the sheet:
  //   ALU
endmodule

module ACC (
  input  [7:0] Data,
  input  Enable,
  input  CLK,
  input  RESET,
  output [7:0] DataOut
);

  Register register_1 (.D(Data), .en(Enable), .clk(CLK), .Q(DataOut), .clr(RESET));

  // Notes on the sheet:
  //   Acumulator
endmodule

module MEMO (
  input  WRITE_REG,
  input  CLK,
  input  [7:0] DataIN,
  input  RESET,
  input  [2:0] RegSelect,
  input  [2:0] OUT_FROM_REG_A,
  input  [2:0] OUT_FROM_REG_B,
  output [7:0] DataOutA,
  output [7:0] DataOutB
);

  wire decoder_1_out0, decoder_1_out1, decoder_1_out2, decoder_1_out3, decoder_1_out4, decoder_1_out5;
  wire [7:0] B_q, C_q, D_q, E_q, H_q, L_q;

  Decoder #(.select(3)) decoder_1 (
    .out0(decoder_1_out0), .out1(decoder_1_out1), .out2(decoder_1_out2), .out3(decoder_1_out3),
    .out4(decoder_1_out4), .out5(decoder_1_out5), .sel(RegSelect), .en(WRITE_REG));  // open: out6, out7
  Register B (.D(DataIN), .en(decoder_1_out0), .clk(CLK), .Q(B_q), .clr(RESET));
  Register D (.D(DataIN), .en(decoder_1_out2), .clk(CLK), .Q(D_q), .clr(RESET));
  Register H (.D(DataIN), .en(decoder_1_out4), .clk(CLK), .Q(H_q), .clr(RESET));
  Register C (.D(DataIN), .en(decoder_1_out1), .clk(CLK), .Q(C_q), .clr(RESET));
  Register E (.D(DataIN), .en(decoder_1_out3), .clk(CLK), .Q(E_q), .clr(RESET));
  Register L (.D(DataIN), .en(decoder_1_out5), .clk(CLK), .Q(L_q), .clr(RESET));
  Multiplexer #(.select(3), .width(8)) multiplexer_1 (
    .in0(B_q), .in1(C_q), .in2(D_q), .in3(E_q), .in4(H_q), .in5(L_q), .out(DataOutB), .sel(OUT_FROM_REG_B));  // open: in6, in7
  Multiplexer #(.select(3), .width(8)) multiplexer_2 (
    .in0(B_q), .in1(C_q), .in2(D_q), .in3(E_q), .in4(H_q), .in5(L_q), .out(DataOutA), .sel(OUT_FROM_REG_A));  // open: in6, in7

  // Notes on the sheet:
  //   B - 000
  //   D - 010
  //   H - 100
  //   C - 001
  //   E - 011
  //   L - 101
  //   Registers Section
endmodule

module CU (
  input  [9:0] Code,
  input  CLK,
  input  RESET,
  output [3:0] ALUCtl,
  output [3:0] RegisterCtl,
  output [1:0] DataBusCtl
);

  Register #(.width(10)) ControlReg (
    .D(Code), .clk(CLK), .Q({DataBusCtl, RegisterCtl, ALUCtl}), .clr(RESET));  // open: en
endmodule

module Z80 (
  input  CLK,
  input  RESET,
  input  [7:0] ExternalData,
  output [7:0] ALU_OUT,
  output [7:0] DATA_OUT_A,
  output [7:0] DATA_OUT_B
);

  wire cuv2_1_write_reg;
  wire [2:0] cuv2_1_reg_h, cuv2_1_reg_l;
  wire [3:3] cuv2_1_alu_op;
  wire [7:0] cuv2_1_data, Program_data;
  wire [15:0] counter_1_q;

  Counter #(.max('hffff), .width(16)) counter_1 (
    .clr(RESET), .clk(CLK), .Q(counter_1_q));  // open: load, up, count, D, carry
  ROM #(.addrWidth(16)) Program (.addr(counter_1_q), .data(Program_data));
  CUv2 cuv2_1 (
    .Code(Program_data), .CLK(CLK), .RESET(RESET), .DATA_REG(DATA_OUT_B), .DATA_MEM(ExternalData),
    .WRITE_REG(cuv2_1_write_reg), .DATA(cuv2_1_data), .REG_H(cuv2_1_reg_h), .REG_L(cuv2_1_reg_l),
    .ALU_OP(cuv2_1_alu_op[3]));
  ALU alu_1 (.DataIN(cuv2_1_data), .ALUCtl({cuv2_1_alu_op[3], 3'b001}), .CLK(CLK), .RESET(RESET), .DataOut(ALU_OUT));
  MEMO memo_1 (
    .WRITE_REG(cuv2_1_write_reg), .CLK(CLK), .DataIN(cuv2_1_data), .RESET(RESET), .RegSelect(cuv2_1_reg_h),
    .OUT_FROM_REG_A(cuv2_1_reg_h), .OUT_FROM_REG_B(cuv2_1_reg_l), .DataOutA(DATA_OUT_A), .DataOutB(DATA_OUT_B));

  // Notes on the sheet:
  //   contents of Program (hex, n*v repeats v):
  //   1e c0 43
  //   Program
  //   Example program
  //   Z80 Main
endmodule

module CUv2 (
  input  [7:0] Code,
  input  CLK,
  input  RESET,
  input  [7:0] DATA_REG,
  input  [7:0] DATA_MEM,
  output WRITE_REG,
  output [7:0] DATA,
  output [2:0] REG_H,
  output [2:0] REG_L,
  output ALU_OP
);

  wire MEM_READ_out, N_TO_R_out, or_1_out, R1_TO_R2_out;
  wire [7:0] I_q, II_q, multiplexer_1_out, multiplexer_2_out, multiplexer_3_out, multiplexer_4_out;
  wire [7:6] III_q;

  Multiplexer #(.width(8)) multiplexer_1 (.in0(DATA_REG), .in1(DATA_MEM), .out(multiplexer_1_out), .sel(MEM_READ_out));
  Multiplexer #(.width(8)) multiplexer_2 (.in0(Code), .in1({8{1'b0}}), .out(multiplexer_2_out), .sel(1'b0));
  Multiplexer #(.width(8)) multiplexer_3 (.in0(I_q), .in1({8{1'b0}}), .out(multiplexer_3_out), .sel(1'b0));
  Multiplexer #(.width(8)) multiplexer_4 (.in0(II_q), .in1({8{1'b0}}), .out(multiplexer_4_out), .sel(or_1_out));
  Multiplexer #(.width(8)) multiplexer_5 (.in0(multiplexer_1_out), .in1(II_q), .out(DATA), .sel(or_1_out));
  or or_1 (or_1_out, N_TO_R_out, ALU_OP);
  Register I (.D(multiplexer_2_out), .clk(CLK), .Q(I_q), .clr(RESET));  // open: en
  Register II (.D(multiplexer_3_out), .clk(CLK), .Q(II_q), .clr(RESET));  // open: en
  Register III (.D(multiplexer_4_out), .clk(CLK), .Q({III_q, REG_H, REG_L}), .clr(RESET));  // open: en
  LED led_1 (.in(III_q[7]));
  LED led_2 (.in(III_q[6]));
  LED led_3 (.in(REG_H[2]));
  LED led_4 (.in(REG_H[1]));
  LED led_5 (.in(REG_H[0]));
  LED led_6 (.in(REG_L[0]));
  LED led_7 (.in(REG_L[2]));
  LED led_8 (.in(REG_L[1]));
  and R1_TO_R2 (R1_TO_R2_out, III_q[6], ~III_q[7]);  // AND_Gate
  and N_TO_R (N_TO_R_out, ~REG_L[0], REG_L[1], REG_L[2], ~III_q[6], ~III_q[7]);  // AND_Gate
  and MEM_READ (MEM_READ_out, ~REG_L[0], REG_L[1], REG_L[2]);  // AND_Gate
  and ALU_N (ALU_OP, ~REG_L[0], REG_L[1], REG_L[2], III_q[6], III_q[7]);  // AND_Gate
  or or_2 (WRITE_REG, R1_TO_R2_out, N_TO_R_out);
endmodule
